# Fritzing sketch BME280-Wiring (saved by Fritzing 0.9.4)
breadboards: 2

parts:
  U1 = ESP32-38PinWide [part_number=ESP32-38PinWide]
  Bauteil2 = BME280
  Bauteil1 = Breadboard Power Supply Board SMD

nets:
  GND: U1.GND, Bauteil2.GND, Bauteil1.GND
  N1: U1.GPIO21, Bauteil2.SDA
  N2: U1.GPIO22, Bauteil2.SCL
  VIN: Bauteil2.VIN, Bauteil1.VCC

notes:
  VCC: 5V
  VCC: 3.3V

custom parts:
  ESP32-38PinWide: Generic 38-Pin ESP32 with wide format (only access to one side of pins on a breadboard) based on Stephen Lilley's HiLetgo ESP-WROOM-32 ESP32 ESP-32S Development Board.
