# Fritzing sketch MH-Z19C (saved by Fritzing 0.9.4)
breadboards: 2

parts:
  Bauteil1 = Breadboard Power Supply Board SMD
  U1 = ESP32-38PinWide [part_number=ESP32-38PinWide]
  TD-er1 = MH-Z19 CO2 sensor [part_number=MH-Z19]

nets:
  GND: Bauteil1.GND, U1.GND
  N1: U1.GPIO36, TD-er1.TX
  N2: U1.GPIO39, TD-er1.RX

notes:
  VCC: 5V
  VCC: 3.3V

custom parts:
  ESP32-38PinWide: Generic 38-Pin ESP32 with wide format (only access to one side of pins on a breadboard) based on Stephen Lilley's HiLetgo ESP-WROOM-32 ESP32 ESP-32S Development Board.
