# Fritzing sketch SDS011 (saved by Fritzing 0.9.4)
breadboards: 2

parts:
  Bauteil1 = Breadboard Power Supply Board SMD
  U1 = ESP32-38PinWide [part_number=ESP32-38PinWide]
  Mod2 = SDS011 - dust sensor [part_number=1]

nets:
  GND: Bauteil1.GND, U1.GND, Mod2.GND
  VCC: Bauteil1.VCC, Mod2.5V
  N1: U1.GPIO34, Mod2.TXD
  N2: U1.GPIO35, Mod2.RXD

notes:
  VCC: 5V
  VCC: 3.3V

custom parts:
  ESP32-38PinWide: Generic 38-Pin ESP32 with wide format (only access to one side of pins on a breadboard) based on Stephen Lilley's HiLetgo ESP-WROOM-32 ESP32 ESP-32S Development Board.
  SDS011 - dust sensor: The SDS 011 Sensor is a quite recent Air Quality Sensor developed by inovafit, a spin-off from the university of Jinan (in Shandong). With its size, it is probably one of the best sensor in terms of accuracy: While other sensors tend to focus on shrinking the sensor size, the SDS 011 has opted for a size tradeoff allowing it to use a larger fan. And the larger the fan, the better the quality.
