# Fritzing sketch TFT-Wiring (saved by Fritzing 0.9.4)
breadboards: 2

parts:
  LCD1 = TFT 1.8 inch 160x128 w SD
  U1 = ESP32-38PinWide [part_number=ESP32-38PinWide]
  YwRobot_Power_Supply1 = YwRobot Breadboard Power Supply [part_number=545043]

nets:
  N1: LCD1.pin_1, YwRobot_Power_Supply1.VCC_5V
  GND: LCD1.pin2, U1.GND, YwRobot_Power_Supply1.GND
  N2: LCD1.pin3, U1.GPIO5
  N3: LCD1.pin4, U1.GPIO17
  N4: LCD1.pin_5, U1.GPIO16
  N5: LCD1.pin_6, U1.GPIO23
  N6: LCD1.pin_7, U1.GPIO18
  N7: LCD1.pin_8, U1.VIN, YwRobot_Power_Supply1.VCC_3.3V

notes:
  VCC: 5V
  VCC: 3.3V
  3.3V
  5V

custom parts:
  TFT 1.8 inch 160x128 w SD: This is a generic 1.8 tft spi lcd display available on ebay and others. The 1.8" display has 128x160 color pixels.
  ESP32-38PinWide: Generic 38-Pin ESP32 with wide format (only access to one side of pins on a breadboard) based on Stephen Lilley's HiLetgo ESP-WROOM-32 ESP32 ESP-32S Development Board.
  YwRobot Breadboard Power Supply: The YwRobot Breadboard Power Supply (MB-V2) has two power rails; they can be 5V or 3V3. Power to the module can be provided through the female USB socket or through the A10 (female) 2.1mm power jack.
