# Fritzing sketch MH-Z19C (saved by Fritzing 0.9.4)
breadboards: 1

parts:
  Bauteil1 = Breadboard Power Supply Board SMD
  U1 = NodeMCU V1.0
  TD-er1 = MH-Z19 CO2 sensor [part_number=MH-Z19]

nets:
  GND: Bauteil1.GND, U1.GND, TD-er1.GND
  VCC: Bauteil1.VCC, TD-er1.Vin
  N1: U1.D0, TD-er1.RX
  N2: U1.D6, TD-er1.TX

notes:
  VCC: 5V
  VCC: 3.3V

custom parts:
  NodeMCU V1.0: ESP8266 based NodeMCU
