# Fritzing sketch SDS011 (saved by Fritzing 0.9.4)
breadboards: 1

parts:
  Mod1 = SDS011 - dust sensor [part_number=1]
  U1 = NodeMCU V1.0
  Bauteil1 = Breadboard Power Supply Board SMD

nets:
  5V: Mod1.5V, Bauteil1.VCC
  GND: Mod1.GND, U1.GND, Bauteil1.GND
  N1: Mod1.RXD, U1.RX
  N2: Mod1.TXD, U1.TX

notes:
  VCC: 5V
  VCC: 3.3V

custom parts:
  SDS011 - dust sensor: The SDS 011 Sensor is a quite recent Air Quality Sensor developed by inovafit, a spin-off from the university of Jinan (in Shandong). With its size, it is probably one of the best sensor in terms of accuracy: While other sensors tend to focus on shrinking the sensor size, the SDS 011 has opted for a size tradeoff allowing it to use a larger fan. And the larger the fan, the better the quality.
  NodeMCU V1.0: ESP8266 based NodeMCU
