# Fritzing sketch Ver2.0 (saved by Fritzing 0.9.4)
circuit board: 8.46667cm x 5.64444cm
breadboards: 2

parts:
  Bauteil1 = Breadboard Power Supply Board SMD
  LCD1 = TFT 1.8 inch 160x128 w SD
  TD-er1 = MH-Z19 CO2 sensor [part_number=MH-Z19]
  Bauteil2 = BME280
  Mod1 = SDS011 - dust sensor [part_number=1]
  U1 = ESP32-38PinWide [part_number=ESP32-38PinWide]

nets:
  GND: Bauteil1.GND, LCD1.pin2, TD-er1.GND, Bauteil2.GND, Mod1.GND, U1.GND
  VIN: Bauteil1.VCC, LCD1.pin_1, LCD1.pin_8, TD-er1.Vin, Bauteil2.VIN, Mod1.5V
  N1: LCD1.pin3, U1.GPIO5
  N2: LCD1.pin4, U1.GPIO17
  N3: LCD1.pin_5, U1.GPIO16
  N4: LCD1.pin_6, U1.GPIO23
  N5: LCD1.pin_7, U1.GPIO18
  N6: TD-er1.RX, U1.GPIO33
  N7: TD-er1.TX, U1.GPIO32
  N8: Bauteil2.SCL, U1.GPIO22
  N9: Bauteil2.SDA, U1.GPIO21
  N10: Mod1.RXD, U1.GPIO26
  N11: Mod1.TXD, U1.GPIO25

notes:
  VCC 3.3V
  VCC 5V

custom parts:
  TFT 1.8 inch 160x128 w SD: This is a generic 1.8 tft spi lcd display available on ebay and others. The 1.8" display has 128x160 color pixels.
  SDS011 - dust sensor: The SDS 011 Sensor is a quite recent Air Quality Sensor developed by inovafit, a spin-off from the university of Jinan (in Shandong). With its size, it is probably one of the best sensor in terms of accuracy: While other sensors tend to focus on shrinking the sensor size, the SDS 011 has opted for a size tradeoff allowing it to use a larger fan. And the larger the fan, the better the quality.
  ESP32-38PinWide: Generic 38-Pin ESP32 with wide format (only access to one side of pins on a breadboard) based on Stephen Lilley's HiLetgo ESP-WROOM-32 ESP32 ESP-32S Development Board.
